# Fritzing sketch 7 segment led (saved by Fritzing 0.9.3b)
breadboards: 1

parts:
  U1 = 7-SEGMENT-DISPLAY [package=7-segment-display]
  R1 = Resistor [tolerance=±5% resistance=330 package=THT]
  R2 = Resistor [tolerance=±5% resistance=330 package=THT]
  R3 = Resistor [tolerance=±5% resistance=330 package=THT]
  R4 = Resistor [tolerance=±5% resistance=330 package=THT]
  R5 = Resistor [tolerance=±5% resistance=330 package=THT]
  R6 = Resistor [tolerance=±5% resistance=330 package=THT]
  R9 = Resistor [tolerance=±5% resistance=330 package=THT]
  U2 = 74HC595 SMD [package="SO16 [SMD]"]  # not connected
  Part1 = Arduino Ethernet Shield (Rev3)
  R10 = Resistor [tolerance=±5% resistance=330 package=THT]

nets:
  N1: U1.E, R3.Pin_0
  N2: U1.D, R4.Pin_0
  N3: U1.G1, R5.Pin_0
  N4: U1.DP, R6.Pin_0
  N5: U1.B, R10.Pin_1
  N6: U1.A, R1.Pin_0
  N7: U1.G2, R9.Pin_0
  N8: U1.F, Part1.5V
  N9: U1.G, R2.Pin_0

// code stored in the sketch: rollDice.ino
/* See NOTICE file for copyright and licensing information */
/* Apache License 2.0 - See Notice*/
/* Copyright 2017, Shaun Ramsey, Chris Saul - See Notice */

/* v0.4 - changed pinMode to digitalWrite to be appropriate, used ! to show they're inverted, added variable roll timers, sped them up */
/* v0.3 - added a function that tests each segment in order A-G,dp */
/* v0.2 - added comments and rearranged some code */


//a map of the digits
static const byte digitMap[] = {
  B00111111, // 0   "0"          AAA        
  B00000110, // 1   "1"         F   B	    
  B01011011, // 2   "2"         F   B
  B01001111, // 3   "3"          GGG
  B01100110, // 4   "4"         E   C
  B01101101, // 5   "5"         E   C
  B01111101, // 6   "6"          DDD
  B00000111, // 7   "7"
  B01111111, // 8   "8"
  B01101111, // 9   "9"
};


//a map of characters
static const byte charMap[] = {
 B01110111, //"a"
 B01111100, //"b"
 B00111001, // 67  'C'
 B01011110, // 68  'd'
 B01111001, // 69  'E'
 B01110001, // 70  'F'
 B00111101, // 71  'G'
 B01110110, // 72  'H'
 B00000110, // 73  'I'
 B00001110, // 74  'J'
 B01110110, // 75  'K'  Same as 'H'
 B00111000, // 76  'L'
 B00000000, // 77  'M'  NO DISPLAY
 B01010100, // 78  'n'
 B00111111, // 79  'O'
 B01110011, // 80  'P'
 B01100111, // 81  'q'
 B01010000, // 82  'r'
 B01101101, // 83  'S'
 B01111000, // 84  't'
 B00111110, // 85  'U'
 B00111110, // 86  'V'  Same as 'U'
 B00000000, // 87  'W'  NO DISPLAY
 B01110110, // 88  'X'  Same as 'H'
 B01101110, // 89  'y'
 B01011011, // 90  'Z'  Same as '2'
};

//map your a-g,dp to pins on the arduino...probably could do this in
//a more orderly fashion but this array allows us to mix things up
                            //a, b, c, d, e, f, g, dp
const int alphaToIndex[] =  {3,  2, 8, 7, 6, 4, 5, 9};//{ 7,6,4,2,1,9,10,5};


const int latchPin = 12;
const int clockPin = 11;
const int dataPin = 13;

//mixed case and some are missing
void displayCharacter(char c) {
   c = tolower(c);
   int index = c - 'a';
   byte d = charMap[index] ^ -1;
   digitalWrite(latchPin, LOW);
   shiftOut(dataPin, clockPin, LSBFIRST, d);
   digitalWrite(latchPin, HIGH);
}


//display this particular digit
void displayDigit(int index, int period) {
   byte d = digitMap[index] ^ -1;
   if (period == HIGH){
    d = d & 127; 
   }
   digitalWrite(latchPin, LOW);
   shiftOut(dataPin, clockPin, LSBFIRST, d);
   digitalWrite(latchPin, HIGH);
}


//not used but useful to turn all the segments off
void turnOffPause(int pause_length) {
  byte d = B00000000;
  digitalWrite(latchPin, LOW);
  delay(pause_length);
  digitalWrite(latchPin, HIGH);
}


//test all the segments
void segmentTest() {
  for(int i = 0; i < 8; i++) {
    byte d = B11111111;
    bitWrite(d, i, 0);
    digitalWrite(latchPin, LOW);
    shiftOut(dataPin, clockPin, LSBFIRST, d);
    digitalWrite(latchPin, HIGH);
    delay(200);
  }
}

// first time - only when botting up does this run
void setup() {
  // init all these pins as output
  pinMode(latchPin, OUTPUT);
  pinMode(clockPin, OUTPUT);
  pinMode(dataPin, OUTPUT);

  //do a segmentTest!
  segmentTest();
  randomSeed(analogRead(0)); //neat way to get a seed
  int ran = random(1,7);  
  int dur = random(1,5);  //makes dice roll feel good
  for(int i = 0; i < ran + 6*dur; i++){
    int k = i % 6 + 1;
    displayDigit(k, LOW);
    delay(15*i + 20);
  }
  displayDigit(ran, HIGH);  //shows the rolled value
}



// loop forever
void loop() {

}
